# Fritzing sketch meshquitto_gateway (saved by Fritzing 0.9.3b)
breadboards: 1

parts:
  MQTT_Gateway = WeMos D1 Mini
  Mesh_Gateway = WeMos D1 Mini

nets:
  N1: MQTT_Gateway.D1, Mesh_Gateway.D2
  N2: MQTT_Gateway.D2, Mesh_Gateway.D1
  N3: MQTT_Gateway.D4, Mesh_Gateway.D5
  N4: MQTT_Gateway.D5, Mesh_Gateway.D4

notes:
  Meshquitto Gateway
