# Fritzing sketch meshquitto_node (saved by Fritzing 0.9.3b)
breadboards: 1

parts:
  WeMos_D1_Mini1 = WeMos D1 Mini
  DS1 = DS18B20 1-Wire Temperature Sensor [part_number=DS18B20]
  LED1 = smd LED [color="Red (633nm)" package="1206 [SMD]"]

nets:
  3V3: WeMos_D1_Mini1.3V3, DS1.VDD
  N1: WeMos_D1_Mini1.D1, LED1.anode
  N2: WeMos_D1_Mini1.D4, DS1.DQ
  N3: WeMos_D1_Mini1.G, DS1.GND, LED1.cathode

notes:
  Meshquitto Node
